# Fritzing sketch joy-pi (saved by Fritzing 0.9.4)
breadboards: 1

parts:
  LEFT = Pushbutton [package="[THT]"]
  RIGHT = Pushbutton [package="[THT]"]
  UP = Pushbutton [package="[THT]"]
  DOWN = Pushbutton [package="[THT]"]
  FIRE = Pushbutton [package="[THT]"]
  R3 = Resistor [tolerance=±5% resistance=10k package=THT]
  R4 = Resistor [tolerance=±5% resistance=10k package=THT]
  R5 = Resistor [tolerance=±5% resistance=10k package=THT]
  R6 = Resistor [tolerance=±5% resistance=10k package=THT]
  R7 = Resistor [tolerance=±5% resistance=10k package=THT]
  MCU1 = Raspberry Pi Zero

nets:
  N1: LEFT.Pin_1, LEFT.Pin_2, RIGHT.Pin_1, RIGHT.Pin_2, UP.Pin_1, UP.Pin_2, DOWN.Pin_1, DOWN.Pin_2, FIRE.Pin_1, FIRE.Pin_2, MCU1.pin_4
  N2: LEFT.Pin_3, LEFT.Pin_4, R6.Pin_0, MCU1.pin_31
  N3: RIGHT.Pin_3, RIGHT.Pin_4, R5.Pin_0, MCU1.pin_37
  N4: UP.Pin_3, UP.Pin_4, R7.Pin_0, MCU1.pin_33
  N5: DOWN.Pin_3, DOWN.Pin_4, R4.Pin_0, MCU1.pin_35
  N6: FIRE.Pin_3, FIRE.Pin_4, R3.Pin_0, MCU1.pin_29
  N7: R3.Pin_1, R4.Pin_1, R5.Pin_1, R6.Pin_1, R7.Pin_1, MCU1.pin_6, MCU1.pin_34
